// Logisim project tme1.circ as structural Verilog: 6 circuits, main circuit main
module main (
  input  a,
  input  b,
  output s
);

  wire not_1_out;

  not not_1 (not_1_out, b);
  and and_1 (s, a, not_1_out, not_1_out);

  // Notes on the sheet:
  //   s=a ET non (b)
endmodule

module mon_xor (
  input  a,
  input  b,
  output s
);

  wire and_1_out, and_2_out, not_1_out, not_2_out;

  not not_1 (not_1_out, a);
  not not_2 (not_2_out, b);
  and and_1 (and_1_out, not_1_out, b);
  and and_2 (and_2_out, a, not_2_out);
  or or_1 (s, and_1_out, and_2_out);

  // Notes on the sheet:
  //   s= a XORb
endmodule

module MUX2 (
  input  e0,
  input  v,
  input  e1,
  output out_4
);

  wire and_1_out, and_2_out, not_1_out;

  not not_1 (not_1_out, v);
  and and_1 (and_1_out, e0, not_1_out);
  and and_2 (and_2_out, v, e1);
  or or_1 (out_4, and_1_out, and_2_out);

  // Notes on the sheet:
  //   l'expression booleenne du multiplexeur ci-desous est  : e0.non(v)+e1.v
endmodule

module MUX2_4 (
  input  in_1,
  input  a0,
  input  a1,
  input  a2,
  input  a3,
  input  b0,
  input  b1,
  input  b2,
  input  b3,
  output out_10,
  output out_11,
  output out_12,
  output out_13
);

  MUX2 mux2_1 (.e0(a0), .v(in_1), .e1(b0), .out_4(out_10));
  MUX2 mux2_2 (.e0(a1), .v(in_1), .e1(b1), .out_4(out_11));
  MUX2 mux2_3 (.e0(a2), .v(in_1), .e1(b2), .out_4(out_12));
  MUX2 mux2_4 (.e0(a3), .v(in_1), .e1(b3), .out_4(out_13));
endmodule

module mux4 (
  input  e0,
  input  i1,
  input  e1,
  input  i0,
  input  e2,
  input  e3,
  output s
);

  wire mux2_1_out_4, mux2_2_out_4;

  MUX2 mux2_1 (.e0(e0), .v(i1), .e1(e1), .out_4(mux2_1_out_4));
  MUX2 mux2_2 (.e0(e2), .v(i1), .e1(e3), .out_4(mux2_2_out_4));
  MUX2 mux2_3 (.e0(mux2_1_out_4), .v(i0), .e1(mux2_2_out_4), .out_4(s));

  // Notes on the sheet:
  //   REPONSE 2 lexpression boolenne dun multiplexeur a 4 entrees
  //   s=non(i0) MUX2(e0,e1)+i0 MUX2(e2,e3)
  //   s=MUX2(MUX2(e0,e1),MUX2(e2,e3))
  //   on a : s=non(i0) i1 e1+non(i0) non(i1) e0+i0 non(i1) e2+i0 i1 e3
  //   s=non(i0)[ i1 e1+ non(i1) e0]+i0[non(i1) e2+i1 e3]
  //   la atille du selecteur doit etre egale a 2bits car on a n=4 entrees et on sait que     2^k-1<n<=2^k  et pour que cette expression soit satisfaite il faut que  k=2 (nombre de bits)
endmodule

module Machine_a_cafe (
  input  sucre,
  input  cafe,
  input  bouillon,
  output out_4
);

  wire and_1_out, and_2_out, not_1_out;

  not not_1 (not_1_out, cafe);
  and and_1 (and_1_out, sucre, not_1_out);
  and and_2 (and_2_out, cafe, bouillon);
  or or_1 (out_4, and_1_out, and_2_out);

  // Notes on the sheet:
  //   s=(cafe ET bouillon) OU (sucre ET non(cafe))
endmodule
