// Logisim project tme2 (1).circ as structural Verilog: 6 circuits, main circuit Addditionneur_1Bit
module Addditionneur_1Bit (
  input  a,
  input  b,
  input  c_in,
  output C_out,
  output Sortie
);

  wire and_1_out, and_2_out, xor_1_out;

  xor xor_1 (xor_1_out, b, c_in);
  and and_1 (and_1_out, b, c_in);
  and and_2 (and_2_out, a, xor_1_out);
  or or_1 (C_out, and_2_out, and_1_out);
  xor xor_2 (Sortie, a, xor_1_out);
endmodule

// add
module Additinneur_4Bits (
  input  cin,
  input  [3:0] A,
  input  [3:0] B,
  output [3:0] sortie,
  output cout
);

  wire addditionneur_1bit_1_c_out, addditionneur_1bit_2_c_out, addditionneur_1bit_3_c_out;

  Addditionneur_1Bit addditionneur_1bit_1 (
    .a(A[0]), .b(B[0]), .c_in(cin), .C_out(addditionneur_1bit_1_c_out), .Sortie(sortie[0]));
  Addditionneur_1Bit addditionneur_1bit_2 (
    .a(A[1]), .b(B[1]), .c_in(addditionneur_1bit_1_c_out), .C_out(addditionneur_1bit_2_c_out),
    .Sortie(sortie[1]));
  Addditionneur_1Bit addditionneur_1bit_3 (
    .a(A[2]), .b(B[2]), .c_in(addditionneur_1bit_2_c_out), .C_out(addditionneur_1bit_3_c_out),
    .Sortie(sortie[2]));
  Addditionneur_1Bit addditionneur_1bit_4 (
    .a(A[3]), .b(B[3]), .c_in(addditionneur_1bit_3_c_out), .C_out(cout), .Sortie(sortie[3]));

  // Notes on the sheet:
  //   b3b2b1b0
  //   +
  //   a3a2a1a0
  //   =s3s2s1s0
  //   l'opperation effectuer est :
endmodule

module Soustracteur_1Bits (
  input  a,
  input  b,
  input  c_in,
  output C_out,
  output Sortie
);

  wire and_1_out, and_2_out, not_1_out, xor_1_out;

  xor xor_1 (xor_1_out, b, c_in);
  not not_1 (not_1_out, a);
  and and_1 (and_1_out, b, c_in);
  and and_2 (and_2_out, not_1_out, xor_1_out);
  or or_1 (C_out, and_2_out, and_1_out);
  xor xor_2 (Sortie, a, xor_1_out);
endmodule

// sous
module Soustracteur_4Bits (
  input  cin,
  input  [3:0] A,
  input  [3:0] B,
  output [3:0] sortie,
  output cout
);

  wire soustracteur_1bits_1_c_out, soustracteur_1bits_2_c_out, soustracteur_1bits_3_c_out;

  Soustracteur_1Bits soustracteur_1bits_1 (
    .a(A[0]), .b(B[0]), .c_in(cin), .C_out(soustracteur_1bits_1_c_out), .Sortie(sortie[0]));
  Soustracteur_1Bits soustracteur_1bits_2 (
    .a(A[1]), .b(B[1]), .c_in(soustracteur_1bits_1_c_out), .C_out(soustracteur_1bits_2_c_out),
    .Sortie(sortie[1]));
  Soustracteur_1Bits soustracteur_1bits_3 (
    .a(A[2]), .b(B[2]), .c_in(soustracteur_1bits_2_c_out), .C_out(soustracteur_1bits_3_c_out),
    .Sortie(sortie[2]));
  Soustracteur_1Bits soustracteur_1bits_4 (
    .a(A[3]), .b(B[3]), .c_in(soustracteur_1bits_3_c_out), .C_out(cout), .Sortie(sortie[3]));

  // Notes on the sheet:
  //   _
  //   l'operation etablie par ce soustracteur et
  //   a3a2a1a0
  //   b3b2b1b0
  //   =s3s2s1s0
endmodule

module Additionneur_avant_simplification (
  input  a,
  input  b,
  input  c_in,
  output sortie,
  output cout
);

  wire and_1_out, and_2_out, and_3_out, and_4_out, and_5_out, and_6_out, and_7_out, and_8_out, not_1_out,
       not_2_out, not_3_out;

  not not_1 (not_1_out, a);
  not not_2 (not_2_out, b);
  not not_3 (not_3_out, c_in);
  and and_1 (and_1_out, not_1_out, not_2_out, c_in);
  and and_2 (and_2_out, not_1_out, b, not_3_out);
  and and_3 (and_3_out, not_2_out, a, not_3_out);
  and and_4 (and_4_out, b, c_in, a);
  and and_5 (and_5_out, b, c_in, a);
  and and_6 (and_6_out, not_1_out, b, c_in);
  and and_7 (and_7_out, a, not_2_out, c_in);
  and and_8 (and_8_out, a, b, not_3_out);
  or or_1 (cout, and_5_out, and_6_out, and_7_out, and_8_out);
  or or_2 (sortie, and_1_out, and_2_out, and_3_out, and_4_out);
endmodule

module Additionneur_Soustracteur_sur_entiers_naturels (
  input  cin,
  input  [3:0] A,
  input  [3:0] B,
  input  Add0_Sub1,
  output CY,
  output [3:0] out_6,
  output BR
);

  wire [3:0] additinneur_4bits_1_sortie, soustracteur_4bits_1_sortie;

  Additinneur_4Bits additinneur_4bits_1 (.cin(cin), .A(A), .B(B), .sortie(additinneur_4bits_1_sortie), .cout(CY));
  Soustracteur_4Bits soustracteur_4bits_1 (.cin(cin), .A(A), .B(B), .sortie(soustracteur_4bits_1_sortie), .cout(BR));
  Multiplexer #(.width(4)) multiplexer_1 (
    .in0(additinneur_4bits_1_sortie), .in1(soustracteur_4bits_1_sortie), .out(out_6), .sel(Add0_Sub1));  // open: en
endmodule
