// Logisim project TME21.circ as structural Verilog: 12 circuits, main circuit a1bit
module a1bit (
  input  a,
  input  b,
  input  cin,
  output s,
  output cout
);

  wire and_1_out, and_2_out, and_3_out, xor_1_out;

  and and_1 (and_1_out, a, b);
  and and_2 (and_2_out, a, cin);
  and and_3 (and_3_out, b, cin);
  xor xor_1 (xor_1_out, a, b);
  xor xor_2 (s, xor_1_out, cin);
  or or_1 (cout, and_1_out, and_2_out, and_3_out);
endmodule

module exo1q1 (
  input  a,
  input  b,
  input  cin,
  output cout,
  output s
);

  wire and_1_out, and_2_out, and_3_out, and_4_out, and_5_out, and_6_out, and_7_out, and_8_out, not_1_out,
       not_2_out, not_3_out;

  not not_1 (not_1_out, a);
  not not_2 (not_2_out, b);
  not not_3 (not_3_out, cin);
  and and_1 (and_1_out, not_1_out, not_2_out, cin);
  and and_2 (and_2_out, not_3_out, not_1_out, b);
  and and_3 (and_3_out, not_3_out, a, not_2_out);
  and and_4 (and_4_out, a, b, cin);
  or or_1 (s, and_1_out, and_2_out, and_3_out, and_4_out);
  and and_5 (and_5_out, not_1_out, b, cin);
  and and_6 (and_6_out, a, not_2_out, cin);
  and and_7 (and_7_out, a, b, not_3_out);
  and and_8 (and_8_out, a, b, cin);
  or or_2 (cout, and_5_out, and_6_out, and_7_out, and_8_out);
endmodule

module addition (
  input  cin,
  input  [3:0] A,
  input  [3:0] B,
  output [3:0] out_4,
  output cout
);

  wire a1bit_1_cout, a1bit_2_cout, a1bit_3_cout;

  a1bit a1bit_1 (.a(A[0]), .b(B[0]), .cin(cin), .s(out_4[0]), .cout(a1bit_1_cout));
  a1bit a1bit_2 (.a(A[1]), .b(B[1]), .cin(a1bit_1_cout), .s(out_4[1]), .cout(a1bit_2_cout));
  a1bit a1bit_3 (.a(A[2]), .b(B[2]), .cin(a1bit_2_cout), .s(out_4[2]), .cout(a1bit_3_cout));
  a1bit a1bit_4 (.a(A[3]), .b(B[3]), .cin(a1bit_3_cout), .s(out_4[3]), .cout(cout));
endmodule

module exo2q2 (
  input  a,
  input  b,
  input  bin,
  output bout,
  output d
);

  wire and_1_out, and_2_out, not_1_out, xor_1_out, xor_2_out;

  not not_1 (not_1_out, a);
  xor xor_1 (xor_1_out, b, bin);
  and and_1 (and_1_out, not_1_out, xor_1_out);
  and and_2 (and_2_out, b, bin);
  xor xor_2 (xor_2_out, b, bin);
  xor xor_3 (d, a, xor_2_out);
  or or_1 (bout, and_1_out, and_2_out);
endmodule

module soustraction (
  input  cin,
  input  [3:0] A,
  input  [3:0] B,
  output [3:0] S,
  output COUT
);

  wire exo2q2_1_bout, exo2q2_2_bout, exo2q2_3_bout;

  exo2q2 exo2q2_1 (.a(A[0]), .b(B[0]), .bin(cin), .bout(exo2q2_1_bout), .d(S[0]));
  exo2q2 exo2q2_2 (.a(A[1]), .b(B[1]), .bin(exo2q2_1_bout), .bout(exo2q2_2_bout), .d(S[1]));
  exo2q2 exo2q2_3 (.a(A[2]), .b(B[2]), .bin(exo2q2_2_bout), .bout(exo2q2_3_bout), .d(S[2]));
  exo2q2 exo2q2_4 (.a(A[3]), .b(B[3]), .bin(exo2q2_3_bout), .bout(COUT), .d(S[3]));
endmodule

module exo3q1 (
  input  cin,
  input  [3:0] A,
  input  [3:0] B,
  input  Add0_Sub1,
  output [3:0] out_5,
  output CY,
  output BR
);

  wire [3:0] addition_1_out_4, soustraction_1_s;

  addition addition_1 (.cin(cin), .A(A), .B(B), .out_4(addition_1_out_4), .cout(CY));
  soustraction soustraction_1 (.cin(cin), .A(A), .B(B), .S(soustraction_1_s), .COUT(BR));
  Multiplexer #(.width(4)) multiplexer_1 (
    .in0(addition_1_out_4), .in1(soustraction_1_s), .out(out_5), .sel(Add0_Sub1));  // open: en
endmodule

module ALU (
  input  [3:0] A,
  input  [3:0] B,
  input  ALUOP,
  output [3:0] out_4,
  output out_5
);

  wire [3:0] multiplexer_1_out, not_1_out;

  assign not_1_out = ~B;  // NOT_Gate not_1, 4 bits wide
  Multiplexer #(.width(4)) multiplexer_1 (.in0(B), .in1(not_1_out), .out(multiplexer_1_out), .sel(ALUOP));  // open: en
  addition addition_1 (.cin(ALUOP), .A(A), .B(multiplexer_1_out), .out_4(out_4), .cout(out_5));
endmodule

module ALU2 (
  input  [3:0] A,
  input  [3:0] B,
  input  ALUOP,
  output [3:0] SORTIE,
  output ZF,
  output SF,
  output CF,
  output OV
);

  wire [3:0] multiplexer_1_out, not_1_out;

  assign not_1_out = ~B;  // NOT_Gate not_1, 4 bits wide
  Multiplexer #(.width(4)) multiplexer_1 (.in0(B), .in1(not_1_out), .out(multiplexer_1_out), .sel(ALUOP));  // open: en
  addual addual_1 (.C(ALUOP), .A(A), .B(multiplexer_1_out), .ZF(ZF), .out_5(SORTIE), .SF(SF), .CF(CF), .OV(OV));
endmodule

module addual (
  input  C,
  input  [3:0] A,
  input  [3:0] B,
  output ZF,
  output [3:0] out_5,
  output SF,
  output CF,
  output OV
);

  wire a1bit_1_cout, a1bit_2_cout, a1bit_3_cout, or_1_out;

  a1bit a1bit_1 (.a(A[0]), .b(B[0]), .cin(C), .s(out_5[0]), .cout(a1bit_1_cout));
  a1bit a1bit_2 (.a(A[1]), .b(B[1]), .cin(a1bit_1_cout), .s(out_5[1]), .cout(a1bit_2_cout));
  a1bit a1bit_3 (.a(A[2]), .b(B[2]), .cin(a1bit_2_cout), .s(out_5[2]), .cout(a1bit_3_cout));
  a1bit a1bit_4 (.a(A[3]), .b(B[3]), .cin(a1bit_3_cout), .s(out_5[3]), .cout(CF));
  or or_1 (or_1_out, out_5[3], out_5[2], OV, out_5[0], out_5[1]);
  xor xor_1 (OV, CF, a1bit_3_cout);
  not not_1 (ZF, or_1_out);

  assign SF = out_5[3];
endmodule

module Decalage_a_droite (
  input  [3:0] in_1,
  input  [1:0] D,
  output [3:0] S
);

  Multiplexer #(.select(2), .width(4)) multiplexer_1 (
    .in0(in_1), .in1({{2{in_1[3]}}, in_1[2:1]}), .in2({{3{in_1[3]}}, in_1[2]}), .in3({4{in_1[3]}}), .out(S),
    .sel(D));  // open: en
endmodule

module Decalage_a_gauche (
  input  [3:0] A,
  input  [1:0] D,
  output [3:0] S
);

  Multiplexer #(.select(2), .width(4)) multiplexer_1 (
    .in0(A), .in1({A[2:0], 1'b0}), .in2({A[1:0], 2'b00}), .in3({A[0], 3'b000}), .out(S), .sel(D));  // open: en
endmodule

module Comparateur (
  input  [3:0] B,
  input  [3:0] A,
  output B_A
);

  wire addual_1_sf, addual_1_zf, or_1_out;

  addual addual_1 (.C(1'b1), .A(B), .B(A), .ZF(addual_1_zf), .SF(addual_1_sf));  // open: out_5, CF, OV
  or or_1 (or_1_out, addual_1_zf, addual_1_sf);
  not not_1 (B_A, or_1_out);
endmodule
