// Logisim project TME4.circ as structural Verilog: 5 circuits, main circuit main
module main (
  input  Din,
  input  WE,
  output Dout
);

  wire CK_out;

  Clock CK (.out(CK_out));
  Register #(.width(1)) register_1 (.D(Din), .en(WE), .Q(Dout), .clk(CK_out), .clr(1'b0));
endmodule

module registre4bits (
  input  [3:0] Din,
  input  WE,
  output [3:0] Dout
);

  wire CK_out;

  Clock CK (.out(CK_out));
  Register #(.width(4)) register_1 (.D(Din), .en(WE), .Q(Dout), .clk(CK_out), .clr(1'b0));
endmodule

module addition3nombres (
  input  [3:0] Din_A,
  input  ext_A,
  input  WE_A,
  input  ALUOP,
  input  [3:0] Din_B,
  input  ext_B,
  input  WE_B,
  input  [1:0] OP_X,
  input  [3:0] Din_C,
  input  ext_C,
  input  WE_C,
  input  [3:0] Din_D,
  input  ext_D,
  input  WE_D,
  input  [1:0] OP_Y,
  output CF,
  output OV,
  output SF,
  output ZF
);

  wire CK_out;
  wire [3:0] alu_1_s, multiplexer_1_out, multiplexer_2_out, multiplexer_3_out, multiplexer_4_out,
       multiplexer_5_out, multiplexer_6_out, register_1_q, register_2_q, register_3_q, register_4_q;

  Multiplexer #(.width(4)) multiplexer_1 (
    .in0(alu_1_s), .in1(Din_A), .out(multiplexer_1_out), .sel(ext_A));  // open: en
  Multiplexer #(.width(4)) multiplexer_2 (
    .in0(alu_1_s), .in1(Din_B), .out(multiplexer_2_out), .sel(ext_B));  // open: en
  Multiplexer #(.width(4)) multiplexer_3 (
    .in0(alu_1_s), .in1(Din_C), .out(multiplexer_3_out), .sel(ext_C));  // open: en
  Multiplexer #(.width(4)) multiplexer_4 (
    .in0(alu_1_s), .in1(Din_D), .out(multiplexer_4_out), .sel(ext_D));  // open: en
  Clock CK (.out(CK_out));
  Register #(.width(4)) register_1 (.D(multiplexer_1_out), .en(WE_A), .Q(register_1_q), .clk(CK_out));  // open: clr
  Register #(.width(4)) register_2 (.D(multiplexer_2_out), .en(WE_B), .Q(register_2_q), .clk(CK_out));  // open: clr
  Register #(.width(4)) register_3 (.D(multiplexer_3_out), .en(WE_C), .Q(register_3_q), .clk(CK_out));  // open: clr
  Register #(.width(4)) register_4 (.D(multiplexer_4_out), .en(WE_D), .Q(register_4_q), .clk(CK_out));  // open: clr
  Multiplexer #(.select(2), .width(4)) multiplexer_5 (
    .in0(register_1_q), .in1(register_2_q), .in2(register_3_q), .in3(register_4_q), .out(multiplexer_5_out),
    .sel(OP_X));  // open: en
  Multiplexer #(.select(2), .width(4)) multiplexer_6 (
    .in0(register_1_q), .in1(register_2_q), .in2(register_3_q), .in3(register_4_q), .out(multiplexer_6_out),
    .sel(OP_Y));  // open: en
  ALU alu_1 (
    .X(multiplexer_5_out), .Y(multiplexer_6_out), .Aluop(ALUOP), .S(alu_1_s), .Cf(CF), .OV(OV), .ZF(ZF),
    .SF(SF));
endmodule

module memoire16mots (
  input  [3:0] in_1,
  input  [7:0] in_2,
  input  in_3,
  input  in_4
);

  wire clock_1_out;
  wire [7:0] ram_1_data;

  Clock clock_1 (.out(clock_1_out));
  RAM #(.addrWidth(4), .bus("separate")) ram_1 (
    .addr(in_1), .din(in_2), .data(ram_1_data), .str(in_3), .clk(clock_1_out), .ld(in_4));  // open: sel, clr
  // Probe on ram_1_data
endmodule

module memoire8mots (
  input  [2:0] in_1,
  input  [3:0] in_2,
  input  in_3,
  input  in_4
);

  wire clock_1_out;
  wire [3:0] ram_1_data;

  Clock clock_1 (.out(clock_1_out));
  RAM #(.addrWidth(3), .dataWidth(4), .bus("separate")) ram_1 (
    .addr(in_1), .din(in_2), .data(ram_1_data), .str(in_3), .clk(clock_1_out), .ld(in_4));  // open: sel, clr
  // Probe on ram_1_data
endmodule
