// Logisim project s3.circ as structural Verilog: 3 circuits, main circuit main
module main (
  input  a,
  input  b,
  input  cin,
  output s,
  output cout
);

  wire and_1_out, and_2_out, xor_1_out;

  and and_1 (and_1_out, a, b);
  xor xor_1 (xor_1_out, a, b);
  xor xor_2 (s, xor_1_out, cin);
  and and_2 (and_2_out, xor_1_out, cin);
  or or_1 (cout, and_1_out, and_2_out);
endmodule

module _4bits (
  input  [3:0] a,
  input  [3:0] b,
  input  cin,
  output [3:0] out_4,
  output cout,
  output OV,
  output ZF,
  output SF
);

  wire and_1_out, and_2_out, and_3_out, main_1_cout, main_2_cout, main_3_cout, not_1_out, not_2_out,
       not_3_out, not_4_out;

  not not_1 (not_1_out, out_4[0]);
  and and_1 (and_1_out, 1'b1, not_1_out);
  and and_2 (and_2_out, and_1_out, not_2_out);
  not not_2 (not_2_out, out_4[1]);
  main main_1 (.a(a[0]), .b(b[0]), .cin(cin), .s(out_4[0]), .cout(main_1_cout));
  and and_3 (and_3_out, and_2_out, not_3_out);
  not not_3 (not_3_out, out_4[2]);
  not not_4 (not_4_out, out_4[3]);
  main main_2 (.a(a[1]), .b(b[1]), .cin(main_1_cout), .s(out_4[1]), .cout(main_2_cout));
  and and_4 (ZF, and_3_out, not_4_out);
  main main_3 (.a(a[2]), .b(b[2]), .cin(main_2_cout), .s(out_4[2]), .cout(main_3_cout));
  main main_4 (.a(a[3]), .b(b[3]), .cin(main_3_cout), .s(out_4[3]), .cout(cout));
  xor xor_1 (OV, cout, main_3_cout);
  and and_5 (SF, 1'b1, out_4[3]);
endmodule

module ALU (
  input  Aluop,
  input  [3:0] X,
  input  [3:0] Y,
  output [3:0] S,
  output Cf,
  output OV,
  output ZF,
  output SF
);

  wire n4bits_2_cout, n4bits_2_ov, n4bits_2_sf, n4bits_2_zf, n4bits_3_cout, n4bits_3_ov, n4bits_3_sf,
       n4bits_3_zf;
  wire [3:0] n4bits_1_out_4, n4bits_2_out_4, n4bits_3_out_4, not_1_out;

  assign not_1_out = ~Y;  // NOT_Gate not_1, 4 bits wide
  _4bits u_4bits_1 (.a(not_1_out), .b(4'b0001), .cin(1'b0), .out_4(n4bits_1_out_4));  // open: cout, OV, ZF, SF
  _4bits u_4bits_2 (
    .a(X), .b(n4bits_1_out_4), .cin(1'b0), .out_4(n4bits_2_out_4), .cout(n4bits_2_cout), .OV(n4bits_2_ov),
    .ZF(n4bits_2_zf), .SF(n4bits_2_sf));
  _4bits u_4bits_3 (
    .a(X), .b(Y), .cin(1'b0), .out_4(n4bits_3_out_4), .cout(n4bits_3_cout), .OV(n4bits_3_ov),
    .ZF(n4bits_3_zf), .SF(n4bits_3_sf));
  Multiplexer #(.width(4), .enable("false")) multiplexer_1 (
    .in0(n4bits_3_out_4), .in1(n4bits_2_out_4), .out(S), .sel(Aluop));
  Multiplexer #(.enable("false")) multiplexer_2 (.in0(n4bits_3_cout), .in1(n4bits_2_cout), .out(Cf), .sel(Aluop));
  Multiplexer #(.enable("false")) multiplexer_3 (.in0(n4bits_3_zf), .in1(n4bits_2_zf), .out(ZF), .sel(Aluop));
  Multiplexer #(.enable("false")) multiplexer_4 (.in0(n4bits_3_ov), .in1(n4bits_2_ov), .out(OV), .sel(Aluop));
  Multiplexer #(.enable("false")) multiplexer_5 (.in0(n4bits_3_sf), .in1(n4bits_2_sf), .out(SF), .sel(Aluop));
endmodule
