// Logisim project CheminDonneesMarep1.circ as structural Verilog: 2 circuits, main circuit main
module main (
  input  CteOutputXEnable,
  input  RegOutputXEnable,
  input  ADOutputXEnable,
  input  DTOutputXEnable,
  input  RegWriteEnable,
  input  ADWriteEnable,
  input  DTWriteEnable,
  input  [1:0] NumRegToRead,
  input  [1:0] NumRegToWrite,
  input  [3:0] Constante,
  input  CteOutputYEnable,
  input  ADOutputYEnable,
  input  DTOutputYEnable,
  input  ADOutputAddressEnable,
  input  clock,
  input  StoreCommand,
  input  LoadCommand,
  output [3:0] ValeurSurDataIn,
  output [3:0] ValeurSurBusX,
  output [3:0] ValeurSurResOut_DataOut,
  output [3:0] ValeurSurBusY,
  output [3:0] ValeurSurBusAdresse
);

  wire [3:0] AD_q, banc_registre_1_readvalue, controlled_buffer_4_out, DT_q;

  assign ValeurSurBusX = CteOutputXEnable ? Constante : 4'bz;  // Controlled_Buffer controlled_buffer_1
  assign ValeurSurBusY = CteOutputYEnable ? Constante : 4'bz;  // Controlled_Buffer controlled_buffer_2
  assign ValeurSurBusX = RegOutputXEnable ? banc_registre_1_readvalue : 4'bz;  // Controlled_Buffer controlled_buffer_3
  assign controlled_buffer_4_out = RegWriteEnable ? ValeurSurResOut_DataOut : 4'bz;  // Controlled_Buffer controlled_buffer_4
  banc_registre banc_registre_1 (
    .NumReadReg(NumRegToRead), .NumWriteReg(NumRegToWrite), .ValueToWrite(controlled_buffer_4_out),
    .Clock(clock), .ReadValue(banc_registre_1_readvalue));
  assign ValeurSurBusX = ADOutputXEnable ? AD_q : 4'bz;  // Controlled_Buffer controlled_buffer_5
  Register #(.width(4)) AD (.D(ValeurSurResOut_DataOut), .en(ADWriteEnable), .Q(AD_q), .clk(clock), .clr(1'b0));
  assign ValeurSurBusY = ADOutputYEnable ? AD_q : 4'bz;  // Controlled_Buffer controlled_buffer_6
  assign ValeurSurBusAdresse = ADOutputAddressEnable ? AD_q : 4'bz;  // Controlled_Buffer controlled_buffer_7
  assign ValeurSurBusX = DTOutputXEnable ? DT_q : 4'bz;  // Controlled_Buffer controlled_buffer_8
  Register #(.width(4)) DT (.D(ValeurSurDataIn), .en(DTWriteEnable), .Q(DT_q), .clk(clock), .clr(1'b0));
  assign ValeurSurBusY = DTOutputYEnable ? DT_q : 4'bz;  // Controlled_Buffer controlled_buffer_9
  Adder #(.width(4)) adder_1 (
    .a(ValeurSurBusX), .b(ValeurSurBusY), .out(ValeurSurResOut_DataOut), .cin(1'b0));  // open: cout
  RAM #(.addrWidth(4), .dataWidth(4), .bus("separate")) ram_1 (
    .addr(ValeurSurBusAdresse), .din(ValeurSurResOut_DataOut), .data(ValeurSurDataIn), .str(StoreCommand),
    .sel(1'b1), .clk(clock), .ld(LoadCommand));  // open: clr

  // Notes on the sheet:
  //   bloc de constantes 4 bits
  //   Exo 3 Question 1
  //   Question 2
  //   Exo 4 Question 1
  //   r[3]<-r[0]+5
  //   Exo5  
  //   bus X
  //   bus Y
  //   IR <- m[PC]
  //   PC <- PC+4
  //   r[2] <- r[0] +2
  //   On les additionne ensuite avec cst = 0
  //   Les tranferts feraient la même chose sur un MIPS
  //   m[r[2]+4]<-r[3]
  //   IR <- m[PC]
  //   PC <- PC+4
  //   r[3]<- r[0]+5
  //   r[2]<- r[0]+4
  //   r[1]<- r[2]+r[3]
  //   AD<-r[2]+4
  //   m[AD]<-r[1]
  //   AD<-r[2]+0
  //   DT<-m[AD]
  //   r[3]<-DT
  //   le regitre 1 contiend 9
  //   le regitre 2 contiend 4
  //   Pour voir le contenu du registre AD (ou DT), 
  //   et on additionne son contenu avec cst = 0
  //   Pour vérifier qu'une opération d'écriture en mémoire à réussi, 
  //   on lit la valeur écrite à son adresse et on l'écrit dans un registre.
  //   1) Transfert non réalisable car contenu de R0 non modifiable par défaut
  //   4) Transfert no réalisable. Il faut d'abord stocker R1 en mémoire.
  //   respectivement   r[2]<- r[0]+4
  //   pour cette instruction on a besoin de 4 transferts 
  //   PC <- PC+4
  //   r[1]<-DT
  //   banc de 4 registres
  //   4 bits
  //   on positionne ADOutXEnable (DTOutXEnable) à 1 et tous les autres à 0
  //   Pour les registres, on séléctionne le numéro du registre en binaire avec NumRegToRead
  //   IR <- m[PC]
  //   AD<-r[2]+4
  //   m[AD]<-r[3]
  //   pour la derniere  instruction de lecture memoire on a besoin de 5 transferts 
  //   IR <- m[PC]
  //   PC <- PC+4
  //   AD<-r[2]+8
  //   DT<-m[AD]
  //   le contenu de la memoire a l'adresse 8(m[8]) et la valeur contenu dans r[1] qui est 9
  //   puis RegWriteEnable et RegReadEnable a 1 pour permettre la lecture et lecriture dans les registre correspondant 
  //   et on met la constante a 5(resp 4) avec CteOutPutEnable a 1 enfin on click 2 fois sur la clock pour avoir le traitement suivant 
  //   Pour la troisieme instruction on doit ecrire a lemplacement memoir de $2+4 le contenu dur registre 3
  //   le regitre 3 contiend la valeur stockée a ladresse memoire 4  (m[4]) qui est initialisee a zero par defaut
  //   Pour la premiere et la deuxième instrucyion on met la valeur de numRegToWrite à 3 (resp 2 ) et la valeur de numREgToRead à 0  
  //   Pour verifier le resultat on a qu'a afficher le contenue des registre comme on a expliqué precedament et pour le contenu de la memoire on fait une lecture 
  //   bus ADRESSE
  //   DATA_IN
  //   RES_OUT
  //   ADD
endmodule

// Banc
module banc_registre (
  input  [3:0] ValueToWrite,
  input  [1:0] NumReadReg,
  input  [1:0] NumWriteReg,
  input  Clock,
  output [3:0] ReadValue
);

  wire decoder_1_out0, decoder_1_out1, decoder_1_out2, decoder_1_out3;
  wire [3:0] R0_q, R1_q, R2_q, R3_q;

  Decoder #(.select(2)) decoder_1 (
    .out0(decoder_1_out0), .out1(decoder_1_out1), .out2(decoder_1_out2), .out3(decoder_1_out3),
    .sel(NumWriteReg), .en(1'b1));
  Register #(.width(4)) R0 (.D(4'b0000), .en(decoder_1_out0), .Q(R0_q), .clk(Clock), .clr(1'b0));
  Register #(.width(4)) R1 (.D(ValueToWrite), .en(decoder_1_out1), .Q(R1_q), .clk(Clock), .clr(1'b0));
  Register #(.width(4)) R2 (.D(ValueToWrite), .en(decoder_1_out2), .Q(R2_q), .clk(Clock), .clr(1'b0));
  Register #(.width(4)) R3 (.D(ValueToWrite), .en(decoder_1_out3), .Q(R3_q), .clk(Clock), .clr(1'b0));
  Multiplexer #(.select(2), .width(4)) multiplexer_1 (
    .in0(R0_q), .in1(R1_q), .in2(R2_q), .in3(R3_q), .out(ReadValue), .sel(NumReadReg));  // open: en
endmodule
