// Logisim project tme2 (1).circ as structural Verilog
module Addditionneur_1Bit (
  input  a,
  input  b,
  input  c_in,
  output C_out,
  output Sortie
);

  wire and_1_out, and_2_out, xor_1_out;

  xor xor_1 (xor_1_out, b, c_in);
  and and_1 (and_1_out, b, c_in);
  and and_2 (and_2_out, a, xor_1_out);
  or or_1 (C_out, and_2_out, and_1_out);
  xor xor_2 (Sortie, a, xor_1_out);
endmodule

// add
module Additinneur_4Bits (
  input  [3:0] b0b1b2b3,
  input  [3:0] a0a1a2a3,
  input  in_3,
  output out_4,
  output [3:0] s0s1s2s3
);

  wire addditionneur_1bit_1_c_out, addditionneur_1bit_2_c_out, addditionneur_1bit_3_c_out;

  Addditionneur_1Bit addditionneur_1bit_1 (
    .a(a0a1a2a3[3]), .b(b0b1b2b3[3]), .c_in(in_3), .C_out(addditionneur_1bit_1_c_out), .Sortie(s0s1s2s3[3]));
  Addditionneur_1Bit addditionneur_1bit_2 (
    .a(a0a1a2a3[2]), .b(b0b1b2b3[2]), .c_in(addditionneur_1bit_1_c_out), .C_out(addditionneur_1bit_2_c_out),
    .Sortie(s0s1s2s3[2]));
  Addditionneur_1Bit addditionneur_1bit_3 (
    .a(a0a1a2a3[1]), .b(b0b1b2b3[1]), .c_in(addditionneur_1bit_2_c_out), .C_out(addditionneur_1bit_3_c_out),
    .Sortie(s0s1s2s3[1]));
  Addditionneur_1Bit addditionneur_1bit_4 (
    .a(a0a1a2a3[0]), .b(b0b1b2b3[0]), .c_in(addditionneur_1bit_3_c_out), .C_out(out_4), .Sortie(s0s1s2s3[0]));

  // Notes on the sheet:
  //   c_out
  //   REMARQUE:
  //   b3b2b1b0
  //   +
  //   a3a2a1a0
  //   =s3s2s1s0
  //   l'opperation effectuer est :
  //   LES BITS D'ETRER ET DE SORTIE SONT MISES DANS L'ORDRE INVERSE
  //   DONC ON FAIT ENTRER a0a1a2a3 et pas a3a2a1a4 
endmodule

module Soustracteur_1Bits (
  input  a,
  input  b,
  input  c_in,
  output C_out,
  output Sortie
);

  wire and_1_out, and_2_out, not_1_out, xor_1_out;

  xor xor_1 (xor_1_out, b, c_in);
  not not_1 (not_1_out, a);
  and and_1 (and_1_out, b, c_in);
  and and_2 (and_2_out, not_1_out, xor_1_out);
  or or_1 (C_out, and_2_out, and_1_out);
  xor xor_2 (Sortie, a, xor_1_out);
endmodule

// sous
module Soustracteur_4Bits (
  input  [3:0] b0b1b2b3,
  input  [3:0] a0a1a2a3,
  input  in_3,
  output c_out,
  output [3:0] s0s1s2s3
);

  wire soustracteur_1bits_1_c_out, soustracteur_1bits_2_c_out, soustracteur_1bits_3_c_out;

  Soustracteur_1Bits soustracteur_1bits_1 (
    .a(a0a1a2a3[3]), .b(b0b1b2b3[3]), .c_in(in_3), .C_out(soustracteur_1bits_1_c_out), .Sortie(s0s1s2s3[3]));
  Soustracteur_1Bits soustracteur_1bits_2 (
    .a(a0a1a2a3[2]), .b(b0b1b2b3[2]), .c_in(soustracteur_1bits_1_c_out), .C_out(soustracteur_1bits_2_c_out),
    .Sortie(s0s1s2s3[2]));
  Soustracteur_1Bits soustracteur_1bits_3 (
    .a(a0a1a2a3[1]), .b(b0b1b2b3[1]), .c_in(soustracteur_1bits_2_c_out), .C_out(soustracteur_1bits_3_c_out),
    .Sortie(s0s1s2s3[1]));
  Soustracteur_1Bits soustracteur_1bits_4 (
    .a(a0a1a2a3[0]), .b(b0b1b2b3[0]), .c_in(soustracteur_1bits_3_c_out), .C_out(c_out), .Sortie(s0s1s2s3[0]));

  // Notes on the sheet:
  //   _
  //   REMARQUE:
  //   l'operation etablie par ce soustracteur et
  //   a3a2a1a0
  //   b3b2b1b0
  //   =s3s2s1s0
  //   LES BITS D'ETRER ET DE SORTIE SONT MISES DANS L'ORDRE INVERSE
  //   DONC ON FAIT ENTRER a0a1a2a3 et pas a3a2a1a4 
endmodule

module Additionneur_avant_simplification (
  input  a,
  input  b,
  input  c_in,
  output sortie,
  output cout
);

  wire and_1_out, and_2_out, and_3_out, and_4_out, and_5_out, and_6_out, and_7_out, not_1_out, not_2_out,
       not_3_out;

  not not_1 (not_1_out, a);
  not not_2 (not_2_out, b);
  not not_3 (not_3_out, c_in);
  and and_1 (and_1_out, not_1_out, not_2_out, c_in);
  and and_2 (and_2_out, not_1_out, b, not_3_out);
  and and_3 (and_3_out, not_2_out, a, not_3_out);
  and and_4 (and_4_out, b, c_in, a);
  and and_5 (and_5_out, not_1_out, b, c_in);
  and and_6 (and_6_out, a, not_2_out, c_in);
  and and_7 (and_7_out, a, b, not_3_out);
  or or_1 (cout, and_4_out, and_5_out, and_6_out, and_7_out);
  or or_2 (sortie, and_1_out, and_2_out, and_3_out, and_4_out);
endmodule

module Additionneur_Soustracteur_sur_entiers_naturels (
  input  cin,
  input  [3:0] in_2,
  input  [3:0] in_3,
  input  Add0_Sub1,
  output CY,
  output [3:0] out_6,
  output BR
);

  wire [3:0] additinneur_4bits_1_s0s1s2s3, soustracteur_4bits_1_s0s1s2s3;

  Additinneur_4Bits additinneur_4bits_1 (
    .b0b1b2b3(in_2), .a0a1a2a3(in_3), .in_3(cin), .s0s1s2s3(additinneur_4bits_1_s0s1s2s3), .out_4(CY));
  Soustracteur_4Bits soustracteur_4bits_1 (
    .b0b1b2b3(in_2), .a0a1a2a3(in_3), .in_3(cin), .s0s1s2s3(soustracteur_4bits_1_s0s1s2s3), .c_out(BR));
  Multiplexer #(.width(4)) multiplexer_1 (
    .in0(additinneur_4bits_1_s0s1s2s3), .in1(soustracteur_4bits_1_s0s1s2s3), .out(out_6), .sel(Add0_Sub1));  // open: en

  // Notes on the sheet:
  //   b0b1b2b3
  //   a0a1a2a3
  //   REMARQUE:
  //   s0s1s2s3
  //   LES BITS D'ETRER ET DE SORTIE SONT MISES DANS L'ORDRE INVERSE
  //   DONC ON FAIT ENTRER a0a1a2a3 et pas a3a2a1a4 
endmodule

module ALU (
  input  [3:0] A,
  input  cin,
  input  [3:0] B,
  input  in_4,
  input  in_5,
  output out_6,
  output [3:0] out_7,
  output out_8,
  output out_9
);

  wire [3:0] additinneur_4bits_1_s0s1s2s3, additinneur_4bits_2_s0s1s2s3, additinneur_4bits_3_s0s1s2s3,
       not_1_out;

  assign not_1_out = ~B;  // NOT_Gate not_1, 4 bits wide
  Additinneur_4Bits additinneur_4bits_1 (
    .b0b1b2b3(A), .a0a1a2a3(B), .in_3(cin), .s0s1s2s3(additinneur_4bits_1_s0s1s2s3), .out_4(out_6));
  Additinneur_4Bits additinneur_4bits_2 (
    .b0b1b2b3(4'b1000), .a0a1a2a3(not_1_out), .in_3(cin), .s0s1s2s3(additinneur_4bits_2_s0s1s2s3),
    .out_4(out_9));
  Additinneur_4Bits additinneur_4bits_3 (
    .b0b1b2b3(A), .a0a1a2a3(additinneur_4bits_2_s0s1s2s3), .in_3(in_5),
    .s0s1s2s3(additinneur_4bits_3_s0s1s2s3), .out_4(out_8));
  Multiplexer #(.width(4)) multiplexer_1 (
    .in0(additinneur_4bits_1_s0s1s2s3), .in1(additinneur_4bits_3_s0s1s2s3), .out(out_7), .sel(in_4));  // open: en

  // Notes on the sheet:
  //   ADD0/SUBB1
endmodule
