// Logisim project tme2.circ as structural Verilog: 6 circuits, main circuit Addditionneur_1Bit
module Addditionneur_1Bit (
  input  a,
  input  b,
  input  c_in,
  output C_out,
  output Sortie
);

  wire and_1_out, and_2_out, xor_1_out;

  xor xor_1 (xor_1_out, b, c_in);
  and and_1 (and_1_out, b, c_in);
  and and_2 (and_2_out, a, xor_1_out);
  or or_1 (C_out, and_2_out, and_1_out);
  xor xor_2 (Sortie, a, xor_1_out);
endmodule

module Additinneur_4Bits (
  input  a0,
  input  b0,
  input  a1,
  input  b1,
  input  a2,
  input  b2,
  input  a3,
  input  b3,
  input  in_9,
  output c_out,
  output s0,
  output s1,
  output s2,
  output s3
);

  wire addditionneur_1bit_1_c_out, addditionneur_1bit_2_c_out, addditionneur_1bit_3_c_out;

  Addditionneur_1Bit addditionneur_1bit_1 (
    .a(b0), .b(a0), .c_in(in_9), .C_out(addditionneur_1bit_1_c_out), .Sortie(s0));
  Addditionneur_1Bit addditionneur_1bit_2 (
    .a(b1), .b(a1), .c_in(addditionneur_1bit_1_c_out), .C_out(addditionneur_1bit_2_c_out), .Sortie(s1));
  Addditionneur_1Bit addditionneur_1bit_3 (
    .a(b2), .b(a2), .c_in(addditionneur_1bit_2_c_out), .C_out(addditionneur_1bit_3_c_out), .Sortie(s2));
  Addditionneur_1Bit addditionneur_1bit_4 (
    .a(b3), .b(a3), .c_in(addditionneur_1bit_3_c_out), .C_out(c_out), .Sortie(s3));
endmodule

module Soustracteur_1Bits (
  input  a,
  input  b,
  input  c_in,
  output C_out,
  output Sortie
);

  wire and_1_out, and_2_out, not_1_out, xor_1_out;

  xor xor_1 (xor_1_out, b, c_in);
  not not_1 (not_1_out, a);
  and and_1 (and_1_out, b, c_in);
  and and_2 (and_2_out, not_1_out, xor_1_out);
  or or_1 (C_out, and_2_out, and_1_out);
  xor xor_2 (Sortie, a, xor_1_out);
endmodule

module Soustracteur_4Bits (
  input  a0,
  input  b0,
  input  a1,
  input  b1,
  input  a2,
  input  b2,
  input  a3,
  input  b3,
  input  in_9,
  output c_out,
  output s0,
  output s1,
  output s2,
  output s3
);

  wire soustracteur_1bits_1_c_out, soustracteur_1bits_2_c_out, soustracteur_1bits_3_c_out;

  Soustracteur_1Bits soustracteur_1bits_1 (
    .a(b0), .b(a0), .c_in(in_9), .C_out(soustracteur_1bits_1_c_out), .Sortie(s0));
  Soustracteur_1Bits soustracteur_1bits_2 (
    .a(b1), .b(a1), .c_in(soustracteur_1bits_1_c_out), .C_out(soustracteur_1bits_2_c_out), .Sortie(s1));
  Soustracteur_1Bits soustracteur_1bits_3 (
    .a(b2), .b(a2), .c_in(soustracteur_1bits_2_c_out), .C_out(soustracteur_1bits_3_c_out), .Sortie(s2));
  Soustracteur_1Bits soustracteur_1bits_4 (
    .a(b3), .b(a3), .c_in(soustracteur_1bits_3_c_out), .C_out(c_out), .Sortie(s3));

  // Notes on the sheet:
  //   l'opperation etablie par ce soustracteur et
  //   b0 b1 b2 b3 - a0 a1 a2 a3 
endmodule

module Additionneur_avant_simplification (
  input  a,
  input  b,
  input  c_in,
  output sortie,
  output cout
);

  wire and_1_out, and_2_out, and_3_out, and_4_out, and_5_out, and_6_out, and_7_out, not_1_out, not_2_out,
       not_3_out;

  not not_1 (not_1_out, a);
  not not_2 (not_2_out, b);
  not not_3 (not_3_out, c_in);
  and and_1 (and_1_out, not_1_out, not_2_out, c_in);
  and and_2 (and_2_out, not_1_out, b, not_3_out);
  and and_3 (and_3_out, not_2_out, a, not_3_out);
  and and_4 (and_4_out, b, c_in, a);
  and and_5 (and_5_out, not_1_out, b, c_in);
  and and_6 (and_6_out, a, not_2_out, c_in);
  and and_7 (and_7_out, a, b, not_3_out);
  or or_1 (cout, and_4_out, and_5_out, and_6_out, and_7_out);
  or or_2 (sortie, and_1_out, and_2_out, and_3_out, and_4_out);
endmodule

module Additionneur_Soustracteur_sur_entiers_naturels (
);

  Additinneur_4Bits additinneur_4bits_1 ();  // open: in_9, a0, b0, a1, b1, a2, b2, a3, b3, s0, s1, s2, s3, c_out
  Multiplexer multiplexer_1 ();  // open: in0, in1, out, sel, en
endmodule
